# Fritzing sketch schematic (saved by Fritzing 0.9.0b)
breadboards: 1

parts:
  Part1 = Arduino Uno (Rev3)
  R1 = Resistor [tolerance=±5% resistance=220 package=THT]
  R2 = Resistor [tolerance=±5% resistance=220 package=THT]
  R3 = Resistor [tolerance=±5% resistance=220 package=THT]
  R4 = Resistor [tolerance=±5% resistance=220 package=THT]
  R5 = Resistor [tolerance=±5% resistance=220 package=THT]
  R6 = Resistor [tolerance=±5% resistance=220 package=THT]

nets:
  N1: Part1.A0, R6.Pin_0
  N2: Part1.A1, R5.Pin_0
  N3: Part1.A2, R4.Pin_0
  N4: Part1.A3, R3.Pin_0
  N5: Part1.A4/SDA, R2.Pin_0
  N6: Part1.A5/SCL, R1.Pin_0

notes:
  TDO
  TCK
  TDI
  RST
  TEST
  GND
  TMS
